// Logisim project adders.circ as structural Verilog
// half_adder
module Half_Adder (
  input  A_input,
  input  B_input,
  output sum,
  output carry
);

  xor xor_1 (sum, A_input, B_input);
  and and_1 (carry, A_input, B_input);
endmodule

module full_adder (
  input  Carry,
  input  A,
  input  B,
  output sum,
  output carry_out
);

  wire half_adder_1_carry, half_adder_1_sum, half_adder_2_carry;

  Half_Adder half_adder_1 (.A_input(A), .B_input(B), .sum(half_adder_1_sum), .carry(half_adder_1_carry));
  Half_Adder half_adder_2 (.A_input(Carry), .B_input(half_adder_1_sum), .sum(sum), .carry(half_adder_2_carry));
  or or_1 (carry_out, half_adder_2_carry, half_adder_1_carry);
endmodule

module _4_bit_adder (
  input  [3:0] in_1,
  input  [3:0] in_2,
  input  in_3,
  output out_4,
  output [3:0] out_5
);

  wire full_adder_1_carry_out, full_adder_3_carry_out, full_adder_4_carry_out;

  full_adder full_adder_1 (
    .Carry(full_adder_3_carry_out), .A(in_2[2]), .B(in_1[2]), .sum(out_5[2]),
    .carry_out(full_adder_1_carry_out));
  full_adder full_adder_2 (.Carry(full_adder_1_carry_out), .A(in_2[3]), .B(in_1[3]), .sum(out_5[3]), .carry_out(out_4));
  full_adder full_adder_3 (
    .Carry(full_adder_4_carry_out), .A(in_2[1]), .B(in_1[1]), .sum(out_5[1]),
    .carry_out(full_adder_3_carry_out));
  full_adder full_adder_4 (.Carry(in_3), .A(in_2[0]), .B(in_1[0]), .sum(out_5[0]), .carry_out(full_adder_4_carry_out));
endmodule
